# Fritzing sketch cub (3) (1) (saved by Fritzing 0.9.10b)

parts:
  U2 = LIPO-2000mAh [package=lipo-2000]
  C1 = TP4056 [chip_label=TP4056 package="DIP (Dual Inline) [THT]"]
  Компонент2 = Adafruit BME280 [part_number="Adafruit #2652"]
  WeMos_D1_Mini1 = WeMos D1 Mini
  C2 = Ceramic Capacitor [capacitance="100 nF" voltage=35V package="0603 [SMD, multilayer]"]
  k1 = Ra-01 - LoRa Module SX1278 [part_number=SX1278]
  C2_2 = Capacitor [package=cap-pth-small]

nets:
  N1: U2.+, C1.pin4
  N2: U2.-, C1.pin5
  3.3V: C1.pin3, Компонент2.3.3V, WeMos_D1_Mini1.3V3, C2.0, k1.3.3V, C2_2.1
  GND: C1.pin6, Компонент2.GND, WeMos_D1_Mini1.G, C2.1, k1.GND, C2_2.2
  N3: Компонент2.SCK/SCL, WeMos_D1_Mini1.D8
  N4: Компонент2.SDI/SDA, WeMos_D1_Mini1.D7
  N5: WeMos_D1_Mini1.D1, k1.SCK
  N6: WeMos_D1_Mini1.D2, k1.MISO
  N7: WeMos_D1_Mini1.D3, k1.MOSI
  N8: WeMos_D1_Mini1.D4, k1.NSS
  N9: WeMos_D1_Mini1.D5, k1.DIO0
  N10: WeMos_D1_Mini1.D6, k1.RESET

notes:
  Аккумулятор Li-Po 1s 2000mAh
  Wemos D1 mini с конденсатором
  Контролер питания TP4056
  Радиомодуль LORA SX1278 (RA-02)
  Датчик атмосферного давления, температуры и влажности воздуха
  BME280

custom parts:
  TP4056: A DIP stand-in part for whatever IC you want. With 6 pins on a 300mil dual inline package (DIP) footprint.
  Adafruit BME280: Bosch has stepped up their game with their new BME280 sensor, an environmental sensor with temperature, barometric pressure and humidity! This sensor is great for all sorts of indoor environmental sensing and can even be used in both I2C and SPI! This precision sensor from Bosch is the best low-cost sensing solution for measuring humidity with ±3% accuracy, barometric pressure with ±1 hPa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
  Ra-01 - LoRa Module SX1278: The Ra-01 LoRa Module featuring the SX1278 engine by Semtech. Module by AI-Thinker. Module (Ra-01) specifications from: https://www.banggood.com/Ra-01-Smart-Electronics-SX1278-LoRa-Spread-Spectrum-Wireless-Module-Ultra-Far-10KM-433M-p-1130769.html Description: Power supply: DC1.8-3.7V(3.3V) Chip: SX1278 Frequency: 433Mhz Operating temperature: -40~+85°C On Sheild Description (may vary by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
